# Fritzing sketch board (saved by Fritzing 0.9.3b)
circuit board: 2.6cm x 1.8cm
breadboards: 1

parts:
  L7805CV = Voltage Regulator - 5V [package="TO220 [THT]"]
  S1 = Toggle Switch [package=THT]
  Vout = female pin header, 2 pins [form="♀ (female)"]
  Vin = Battery
  C1 = Ceramic Capacitor [capacitance=10µF voltage=16V package="100 mil [THT, multilayer]"]
  C2 = Ceramic Capacitor [capacitance=10µF voltage=16V package="100 mil [THT, multilayer]"]

nets:
  N1: L7805CV.input_voltage, S1.L1, C2.1
  N2: L7805CV.GND, Vout.pin2, Vin.-, C1.0, C2.0
  N3: L7805CV.output_voltage, Vout.pin1, C1.1
  N4: S1.COM, Vin.+

notes:
  Katje
  +
  -
  W.A. ten Brink
